// Logisim project Automaton.circ as structural Verilog: 3 circuits, main circuit Automaton
module Top (
  input  [7:0] Seed,
  input  [7:0] Rule,
  input  Rst
);

  wire clock_1_out, Init_q;
  wire [7:0] automaton_1_out0, multiplexer_1_out, register_1_q;

  Clock clock_1 (.out(clock_1_out));
  D_Flip_Flop Init (.D(1'b1), .clk(clock_1_out), .Q(Init_q), .reset(Rst));  // open: Qn, preset
  // Probe on multiplexer_1_out
  Multiplexer #(.width(8), .enable("false")) multiplexer_1 (
    .in0(Seed), .in1(register_1_q), .out(multiplexer_1_out), .sel(Init_q));
  // Probe on automaton_1_out0
  Automaton automaton_1 (.In0(multiplexer_1_out), .Rule(Rule), .out0(automaton_1_out0));
  Register register_1 (.D(automaton_1_out0), .en(1'b1), .clk(clock_1_out), .Q(register_1_q), .clr(Rst));
  DotMatrix #(.inputtype("row"), .matrixcols(1), .matrixrows(8)) dotmatrix_1 (
    .row0(automaton_1_out0[7]), .row1(automaton_1_out0[6]), .row2(automaton_1_out0[5]),
    .row3(automaton_1_out0[4]), .row4(automaton_1_out0[3]), .row5(automaton_1_out0[2]),
    .row6(automaton_1_out0[1]), .row7(automaton_1_out0[0]));

  // Notes on the sheet:
  //   @adumont
  //   8bit Cellular Automaton
endmodule

module Automaton (
  input  [7:0] In0,
  input  [7:0] Rule,
  output [7:0] out0
);

  aBlock B0 (.Rule(Rule), .i0(In0[7]), .i1(In0[0]), .i2(In0[1]), .o(out0[0]));
  aBlock B1 (.Rule(Rule), .i0(In0[0]), .i1(In0[1]), .i2(In0[2]), .o(out0[1]));
  aBlock B2 (.Rule(Rule), .i0(In0[1]), .i1(In0[2]), .i2(In0[3]), .o(out0[2]));
  aBlock B3 (.Rule(Rule), .i0(In0[2]), .i1(In0[3]), .i2(In0[4]), .o(out0[3]));
  aBlock B4 (.Rule(Rule), .i0(In0[3]), .i1(In0[4]), .i2(In0[5]), .o(out0[4]));
  aBlock B5 (.Rule(Rule), .i0(In0[4]), .i1(In0[5]), .i2(In0[6]), .o(out0[5]));
  aBlock B6 (.Rule(Rule), .i0(In0[5]), .i1(In0[6]), .i2(In0[7]), .o(out0[6]));
  aBlock B7 (.Rule(Rule), .i0(In0[6]), .i1(In0[7]), .i2(In0[0]), .o(out0[7]));
endmodule

module aBlock (
  input  [7:0] Rule,
  input  i0,
  input  i1,
  input  i2,
  output o
);

  // Probe on {i2, i1, i0}
  BitSelector bitselector_1 (.in(Rule), .out(o), .sel({i2, i1, i0}));
endmodule
